// Logisim project SD_Group07.circ as structural Verilog: 4 circuits, main circuit main
module main (
  input  in_1,
  output [11:0] pc,
  output [11:0] r0,
  output [11:0] r1,
  output [11:0] r2,
  output [11:0] r3,
  output [11:0] r4,
  output [11:0] r5,
  output [11:0] r6,
  output [11:0] r7,
  output [3:0] out_11,
  output [11:0] out_12,
  output [2:0] out_13,
  output [2:0] out_14,
  output [2:0] out_15,
  output [11:0] out_16,
  output halt
);

  wire and_1_out, control_logic_1_alu_source, control_logic_1_memread, control_logic_1_memtoreg,
       control_logic_1_memwrite, control_logic_1_regwrite, not_1_out, reset_out;
  wire [3:0] control_logic_1_alu;
  wire [11:0] bit_extender_1_out, multiplexer_1_out, program_counter_1_out_6, ram_2_data, register_file_1_p8,
       register_file_1_p9;

  Halt halt_1 (.instruction({out_11, out_13, out_14, out_15}), .clock(in_1), .reset(reset_out), .halt(halt));
  Clock clock_1 ();  // open: out
  Button reset (.out(reset_out));
  and and_1 (and_1_out, ~halt, in_1);  // AND_Gate
  program_counter program_counter_1 (
    .Branch_relative(1'b0), .Branch_absolute(1'b0), .C(and_1_out), .Reset(1'b0),
    .out_6(program_counter_1_out_6));  // open: Branch_value
  Control_Logic control_logic_1 (
    .in_1({out_11, out_13, out_14, out_15}), .RegWrite(control_logic_1_regwrite),
    .MemToReg(control_logic_1_memtoreg), .MemWrite(control_logic_1_memwrite),
    .MemRead(control_logic_1_memread), .ALU(control_logic_1_alu), .ALU_Source(control_logic_1_alu_source));
  RAM #(.addrWidth(12), .dataWidth(13)) ram_1 (
    .addr(program_counter_1_out_6), .data({out_11, out_13, out_14, out_15}), .sel(1'b1), .clk(and_1_out),
    .ld(1'b1), .clr(1'b0));
  assign bit_extender_1_out = {{9{1'b0}}, out_15};  // Bit_Extender bit_extender_1
  // register_file register_file_1: pin names not known; wires that end beside it: out_14, out_15, out_13, out_12, control_logic_1_regwrite, and_1_out, 1'b0, register_file_1_p8, register_file_1_p9
  Multiplexer #(.width(12), .enable("false")) multiplexer_1 (
    .in0(register_file_1_p9), .in1(bit_extender_1_out), .out(multiplexer_1_out),
    .sel(control_logic_1_alu_source));
  _12_bit_ALU u_12_bit_alu_1 (
    .ALU_code(control_logic_1_alu), .a(register_file_1_p8), .b(multiplexer_1_out), .result(out_16));  // open: overflow
  not not_1 (not_1_out, control_logic_1_memtoreg);
  RAM #(.addrWidth(12), .dataWidth(12), .bus("separate")) ram_2 (
    .addr(out_16), .din(register_file_1_p9), .data(ram_2_data), .str(control_logic_1_memwrite), .sel(1'b1),
    .clk(and_1_out), .ld(control_logic_1_memread), .clr(1'b0));
  Multiplexer #(.width(12), .enable("false")) multiplexer_2 (
    .in0(ram_2_data), .in1(out_16), .out(out_12), .sel(not_1_out));

  // Notes on the sheet:
  //   current instruction
  //   clock signal
  //   reset button
  //   RegWrite
  //   DO NOT CHANGE THE INPUTS AND OUTPUTS OF THIS CIRCUIT! Do not add/remove inputs or outputs. Do not even change their location or orientation.
  //   MemToReg
  //   Memwrite
  //   Memread
endmodule

module Halt (
  input  [12:0] instruction,
  input  clock,
  input  reset,
  output halt
);

  wire and_1_out, comparator_1_eq, comparator_2_gt, counter_1_carry, or_1_out, or_2_out;
  wire [11:0] counter_1_q;

  Comparator #(.width(13), .mode("unsigned")) comparator_1 (
    .a(instruction), .b({13{1'b0}}), .eq(comparator_1_eq));  // open: gt, lt
  Counter #(.width(12), .max('hfff), .trigger("falling")) counter_1 (
    .Q(counter_1_q), .carry(counter_1_carry), .clk(clock), .clr(reset));  // open: load, D, count
  or or_1 (or_1_out, comparator_1_eq, counter_1_carry);
  Comparator #(.width(12), .mode("unsigned")) comparator_2 (
    .a(counter_1_q), .b({12{1'b0}}), .gt(comparator_2_gt));  // open: eq, lt
  or or_2 (or_2_out, halt, and_1_out);
  and and_1 (and_1_out, or_1_out, comparator_2_gt);
  Register #(.width(1)) register_1 (.D(or_2_out), .Q(halt), .clk(clock), .clr(reset));  // open: en

  // Notes on the sheet:
  //   halt becomes and stays asserted if the instruction is 0000 (not in the first clock cycle) or the end of the counter is reached (2^12)
endmodule

module program_counter (
  input  Branch_relative,
  input  Branch_absolute,
  input  [11:0] Branch_value,
  input  C,
  input  Reset,
  output [11:0] out_6
);

  wire and_1_out;
  wire [1:0] priority_encoder_1_out;
  wire [11:0] multiplexer_1_out, n12bit_cla_1_p5, n12bit_cla_2_p4;

  // _12bit_CLA 12bit_cla_1: pin names not known; wires that end beside it: Reset, Branch_value, out_6, 1'b0, n12bit_cla_1_p5
  and and_1 (and_1_out, ~Branch_relative, ~Branch_absolute);  // AND_Gate
  Priority_Encoder #(.select(2)) priority_encoder_1 (
    .in0(Branch_relative), .in1(Branch_absolute), .in2(and_1_out), .out(priority_encoder_1_out));  // open: in3, gs, en_out, en_in
  Multiplexer #(.select(2), .width(12), .enable("false")) multiplexer_1 (
    .in0(n12bit_cla_1_p5), .in1(Branch_value), .in2(n12bit_cla_2_p4), .out(multiplexer_1_out),
    .sel(priority_encoder_1_out));  // open: in3
  _12bit_register u_12bit_register_1 (.Input(multiplexer_1_out), .Reset(Reset), .Write(1'b1), .Clock(C), .out_5(out_6));
  // _12bit_CLA 12bit_cla_2: pin names not known; wires that end beside it: out_6, 12'h1, 1'b0, n12bit_cla_2_p4
endmodule

module Control_Logic (
  input  [12:0] in_1,
  output RegWrite,
  output MemToReg,
  output MemWrite,
  output MemRead,
  output [3:0] ALU,
  output ALU_Source
);

  wire and_1_out, and_2_out, not_1_out, not_2_out, not_3_out, not_4_out, not_5_out, not_7_out, not_8_out,
       not_9_out, or_1_out;
  wire [3:0] bit_extender_1_out, multiplexer_1_out;

  assign bit_extender_1_out = {{1{1'b1}}, in_1[2:0]};  // Bit_Extender bit_extender_1
  not not_1 (not_1_out, in_1[9]);
  not not_2 (not_2_out, in_1[10]);
  not not_3 (not_3_out, in_1[11]);
  not not_4 (not_4_out, in_1[12]);
  and and_1 (and_1_out, not_1_out, not_2_out, not_3_out, not_4_out);
  and and_2 (and_2_out, ~and_1_out, ~MemRead, ~MemWrite);  // AND_Gate
  not not_5 (not_5_out, and_2_out);
  Multiplexer #(.width(4), .enable("false")) multiplexer_1 (
    .in0(in_1[12:9]), .in1(bit_extender_1_out), .out(multiplexer_1_out), .sel(not_5_out));
  and and_3 (MemRead, in_1[9], not_2_out, not_3_out, in_1[12]);
  and and_4 (MemWrite, not_1_out, in_1[10], not_3_out, in_1[12]);
  not not_6 (RegWrite, MemWrite);
  not not_7 (not_7_out, MemRead);
  not not_8 (not_8_out, and_2_out);
  not not_9 (not_9_out, and_1_out);
  or or_1 (or_1_out, MemRead, MemWrite);
  Multiplexer #(.width(4), .enable("false")) multiplexer_2 (
    .in0(multiplexer_1_out), .in1(4'b0011), .out(ALU), .sel(or_1_out));
  or or_2 (ALU_Source, MemWrite, MemRead);

  assign MemToReg = MemRead;

  // Notes on the sheet:
  //   Unary
  //   Binary
  //   Lw
  //   Sw
endmodule
